// Digital circuit BasicReg8.dig as structural Verilog
module BasicReg8 (
  input  E,
  input  CLK,
  input  [7:0] D,
  output [7:0] Q
);

  Register #(.Bits(8)) reg8 (.D(D), .C(CLK), .en(E), .Q(Q));
endmodule
