// Digital circuit TesteCpuDidatica.dig as structural Verilog
module TesteCpuDidatica (
  input  Clock,
  input  Reset,
  output a,
  output b,
  output c,
  output d,
  output e,
  output f,
  output g,
  output dig0,
  output dig1
);

  wire cpu8bit1k_1_oute, div50m10hz_1_y;
  wire [3:0] multiplexer_1_out;
  wire [7:0] basicreg8_1_q, cpu8bit1k_1_out;

  DIV50M10HZ div50m10hz_1 (.Clock50M(Clock), .y(div50m10hz_1_y));
  CPU8Bit1K cpu8bit1k_1 (
    .Reset(Reset), .IN({8{1'b0}}), .Clock(div50m10hz_1_y), .OUT(cpu8bit1k_1_out), .OutE(cpu8bit1k_1_oute));  // open: AddrBus, InE
  BasicReg8 basicreg8_1 (.Q(basicreg8_1_q), .D(cpu8bit1k_1_out), .E(cpu8bit1k_1_oute), .CLK(div50m10hz_1_y));
  DIV50M100HZ div50m100hz_1 (.Clock50M(Clock), .y(dig0));
  Multiplexer #(.Bits(4)) multiplexer_1 (
    .sel(dig0), .in_0(basicreg8_1_q[3:0]), .in_1(basicreg8_1_q[7:4]), .out(multiplexer_1_out));
  Driver7Seg driver7seg_1 (
    .D0(multiplexer_1_out[0]), .D1(multiplexer_1_out[1]), .D2(multiplexer_1_out[2]),
    .D3(multiplexer_1_out[3]), .Inv(1'b1), .a(a), .b(b), .c(c), .d(d), .e(e), .f(f), .g(g));
  not not_1 (dig1, dig0);

  // Notes on the sheet:
  //   Clock: Hz: 10
endmodule
